// Logisim project Vers2.circ as structural Verilog
module FourBitSyncCounter (
  input  D3,
  input  D2,
  input  D1,
  input  D0,
  input  PE,
  input  CEP,
  input  CET,
  input  CP,
  input  MR,
  output Q0,
  output Q1,
  output Q2,
  output Q3,
  output TC
);

  wire and_1_out, and_2_out, C1_out, C2_out, C3_out, EN_out, multiplexer_1_out, multiplexer_2_out,
       multiplexer_3_out, multiplexer_4_out, multiplexer_5_out, multiplexer_6_out, multiplexer_7_out,
       multiplexer_8_out, not_1_out, X0_out, X1_out, X2_out, X3_out;

  D_Flip_Flop FF0 (.D(multiplexer_2_out), .clk(CP), .Q(Q0), .reset(not_1_out));  // open: Qn, preset
  not not_1 (not_1_out, MR);
  D_Flip_Flop FF1 (.D(multiplexer_4_out), .clk(CP), .Q(Q1), .reset(not_1_out));  // open: Qn, preset
  and EN (EN_out, CEP, CET);
  D_Flip_Flop FF2 (.D(multiplexer_6_out), .clk(CP), .Q(Q2), .reset(not_1_out));  // open: Qn, preset
  Multiplexer multiplexer_1 (.in0(D0), .in1(Q0), .out(multiplexer_1_out), .sel(PE));
  Multiplexer multiplexer_2 (.in0(multiplexer_1_out), .in1(X0_out), .out(multiplexer_2_out), .sel(EN_out));
  D_Flip_Flop FF3 (.D(multiplexer_8_out), .clk(CP), .Q(Q3), .reset(not_1_out));  // open: Qn, preset
  and C1 (C1_out, Q0, EN_out);
  xor X0 (X0_out, EN_out, Q0);
  and and_1 (and_1_out, Q0, Q1);
  and and_2 (and_2_out, Q2, Q3);
  Multiplexer multiplexer_3 (.in0(D1), .in1(Q1), .out(multiplexer_3_out), .sel(PE));
  Multiplexer multiplexer_4 (.in0(multiplexer_3_out), .in1(X1_out), .out(multiplexer_4_out), .sel(EN_out));
  and C2 (C2_out, C1_out, Q1);
  xor X1 (X1_out, C1_out, Q1);
  and and_3 (TC, and_2_out, and_1_out, CET);
  Multiplexer multiplexer_5 (.in0(D2), .in1(Q2), .out(multiplexer_5_out), .sel(PE));
  Multiplexer multiplexer_6 (.in0(multiplexer_5_out), .in1(X2_out), .out(multiplexer_6_out), .sel(EN_out));
  and C3 (C3_out, C2_out, Q2);
  xor X2 (X2_out, C2_out, Q2);
  xor X3 (X3_out, C3_out, Q3);
  Multiplexer multiplexer_7 (.in0(D3), .in1(Q3), .out(multiplexer_7_out), .sel(PE));
  Multiplexer multiplexer_8 (.in0(multiplexer_7_out), .in1(X3_out), .out(multiplexer_8_out), .sel(EN_out));
endmodule

module SL161 (
  input  D3,
  input  D2,
  input  D1,
  input  D0,
  input  PE,
  input  CEP,
  input  CET,
  input  CP,
  input  MR,
  output Q0,
  output Q1,
  output Q2,
  output Q3,
  output TC
);

  wire and_1_out, and_2_out, C1_out, C2_out, C3_out, EN_out, multiplexer_1_out, multiplexer_2_out,
       multiplexer_3_out, multiplexer_4_out, multiplexer_5_out, multiplexer_6_out, multiplexer_7_out,
       multiplexer_8_out, not_1_out, X0_out, X1_out, X2_out, X3_out;

  D_Flip_Flop FF0 (.D(multiplexer_2_out), .clk(CP), .Q(Q0), .reset(not_1_out));  // open: Qn, preset
  not not_1 (not_1_out, MR);
  D_Flip_Flop FF1 (.D(multiplexer_4_out), .clk(CP), .Q(Q1), .reset(not_1_out));  // open: Qn, preset
  and EN (EN_out, CEP, CET);
  D_Flip_Flop FF2 (.D(multiplexer_6_out), .clk(CP), .Q(Q2), .reset(not_1_out));  // open: Qn, preset
  Multiplexer multiplexer_1 (.in0(D0), .in1(Q0), .out(multiplexer_1_out), .sel(PE));
  Multiplexer multiplexer_2 (.in0(multiplexer_1_out), .in1(X0_out), .out(multiplexer_2_out), .sel(EN_out));
  D_Flip_Flop FF3 (.D(multiplexer_8_out), .clk(CP), .Q(Q3), .reset(not_1_out));  // open: Qn, preset
  and C1 (C1_out, Q0, EN_out);
  xor X0 (X0_out, EN_out, Q0);
  and and_1 (and_1_out, Q0, Q1);
  and and_2 (and_2_out, Q2, Q3);
  Multiplexer multiplexer_3 (.in0(D1), .in1(Q1), .out(multiplexer_3_out), .sel(PE));
  Multiplexer multiplexer_4 (.in0(multiplexer_3_out), .in1(X1_out), .out(multiplexer_4_out), .sel(EN_out));
  and C2 (C2_out, C1_out, Q1);
  xor X1 (X1_out, C1_out, Q1);
  and and_3 (TC, and_2_out, and_1_out, CET);
  Multiplexer multiplexer_5 (.in0(D2), .in1(Q2), .out(multiplexer_5_out), .sel(PE));
  Multiplexer multiplexer_6 (.in0(multiplexer_5_out), .in1(X2_out), .out(multiplexer_6_out), .sel(EN_out));
  and C3 (C3_out, C2_out, Q2);
  xor X2 (X2_out, C2_out, Q2);
  xor X3 (X3_out, C3_out, Q3);
  Multiplexer multiplexer_7 (.in0(D3), .in1(Q3), .out(multiplexer_7_out), .sel(PE));
  Multiplexer multiplexer_8 (.in0(multiplexer_7_out), .in1(X3_out), .out(multiplexer_8_out), .sel(EN_out));
endmodule

module Horizontal_Sync (
  input  CLK,
  input  DataBits,
  input  in_3,
  output HSync,
  output HBlank,
  output Bit264,
  output q00,
  output q01,
  output q02,
  output q03,
  output q04,
  output q05,
  output q06,
  output q07,
  output q08
);

  wire n7400_1_pin3, n7400_1_pin12, n7404_2_pin6, n7430_1_pin1, n7430_1_pin2, n7430_1_pin3, n7430_1_pin5,
       n7430_1_pin6, n7430_1_pin8, n7430_2_pin4, n7430_2_pin8, n7430_3_pin8, n7430_4_pin6, n7430_4_pin11,
       U1_pin7, U1_pin15, U2_pin15;

  // Probe on q00
  _74161 U1 (
    .pin1(Bit264), .pin2(CLK), .pin3(DataBits), .pin4(DataBits), .pin5(DataBits), .pin6(DataBits),
    .pin7(U1_pin7), .pin15(U1_pin15), .pin14(q00), .pin13(q01), .pin12(q02), .pin11(q03), .pin10(U1_pin7),
    .pin9(U1_pin7));
  // Probe on q01
  _7430 u_7430_1 (
    .pin1(n7430_1_pin1), .pin2(n7430_1_pin2), .pin3(n7430_1_pin3), .pin4(q03), .pin5(n7430_1_pin5),
    .pin6(n7430_1_pin6), .pin12(q07), .pin11(q06), .pin8(n7430_1_pin8));  // open: pin13, pin10, pin9
  // Probe on q02
  // Probe on q03
  // Probe on q04
  _74161 U2 (
    .pin1(Bit264), .pin2(CLK), .pin3(in_3), .pin4(in_3), .pin5(in_3), .pin6(in_3), .pin7(U1_pin15),
    .pin15(U2_pin15), .pin14(q04), .pin13(q05), .pin12(q06), .pin11(q07), .pin10(U1_pin15), .pin9(U1_pin7));
  _7430 u_7430_2 (
    .pin1(n7430_1_pin1), .pin2(q01), .pin3(n7430_1_pin3), .pin4(n7430_2_pin4), .pin5(q04),
    .pin6(n7430_1_pin5), .pin12(q07), .pin11(q06), .pin8(n7430_2_pin8));  // open: pin13, pin10, pin9
  // Probe on q05
  // Probe on q06
  // Probe on q07
  // Probe on q08
  _7430 u_7430_3 (
    .pin1(n7430_1_pin1), .pin2(q01), .pin3(n7430_1_pin3), .pin4(n7430_2_pin4), .pin5(q04), .pin6(q05),
    .pin12(q07), .pin11(q06), .pin8(n7430_3_pin8));  // open: pin13, pin10, pin9
  _7404 u_7404_1 (
    .pin1(q00), .pin2(n7430_1_pin1), .pin3(q01), .pin4(n7430_1_pin2), .pin5(q02), .pin6(n7430_1_pin3),
    .pin13(q03), .pin12(n7430_2_pin4), .pin11(q04), .pin10(n7430_1_pin5), .pin9(q05), .pin8(n7430_1_pin6));
  _74161 U3 (
    .pin1(Bit264), .pin2(CLK), .pin3(in_3), .pin4(in_3), .pin5(in_3), .pin6(in_3), .pin7(U2_pin15),
    .pin14(q08), .pin10(U2_pin15), .pin9(U1_pin7));  // open: pin15, pin13, pin12, pin11
  _7430 u_7430_4 (
    .pin1(n7430_1_pin2), .pin2(n7430_1_pin3), .pin3(q03), .pin4(n7430_1_pin5), .pin5(n7430_1_pin6),
    .pin6(n7430_4_pin6), .pin12(q08), .pin11(n7430_4_pin11), .pin8(Bit264));  // open: pin13, pin10, pin9
  _7404 u_7404_2 (
    .pin1(q06), .pin2(n7430_4_pin6), .pin3(q07), .pin4(n7430_4_pin11), .pin5(q08), .pin6(n7404_2_pin6));  // open: pin13, pin12, pin11, pin10, pin9, pin8
  _7400 u_7400_1 (
    .pin1(n7430_2_pin8), .pin2(HSync), .pin3(n7400_1_pin3), .pin4(n7400_1_pin3), .pin5(n7430_3_pin8),
    .pin6(HSync), .pin13(Bit264), .pin12(n7400_1_pin12), .pin11(HBlank), .pin10(n7430_1_pin8), .pin9(HBlank),
    .pin8(n7400_1_pin12));
  // also tied to VCC on the sheet: U1_pin7
endmodule

module Vertical_Sync (
  input  CLK,
  input  DataBits,
  output VSync,
  output VBlank,
  output q00,
  output q01,
  output q02,
  output q03,
  output q04,
  output q05,
  output q06,
  output q07,
  output q08,
  output q09
);

  wire n7400_1_pin3, n7400_1_pin12, n7430_1_pin4, n7430_1_pin5, n7430_1_pin6, n7430_1_pin8, n7430_1_pin11,
       n7430_2_pin8, n7430_3_pin6, n7430_3_pin8, U1_pin1, U1_pin7, U1_pin15, U2_pin15;

  // Probe on q00
  _74161 U1 (
    .pin1(U1_pin1), .pin2(CLK), .pin3(DataBits), .pin4(DataBits), .pin5(DataBits), .pin6(DataBits),
    .pin7(U1_pin7), .pin15(U1_pin15), .pin14(q00), .pin13(q01), .pin12(q02), .pin11(q03), .pin10(U1_pin7),
    .pin9(U1_pin7));
  // Probe on q01
  _7430 u_7430_1 (
    .pin1(q04), .pin2(q06), .pin3(q08), .pin4(n7430_1_pin4), .pin5(n7430_1_pin5), .pin6(n7430_1_pin6),
    .pin12(q03), .pin11(n7430_1_pin11), .pin8(n7430_1_pin8));  // open: pin13, pin10, pin9
  // Probe on q02
  // Probe on q03
  // Probe on q04
  _74161 U2 (
    .pin1(U1_pin1), .pin2(CLK), .pin3(DataBits), .pin4(DataBits), .pin5(DataBits), .pin6(DataBits),
    .pin7(U1_pin15), .pin15(U2_pin15), .pin14(q04), .pin13(q05), .pin12(q06), .pin11(q07), .pin10(U1_pin15),
    .pin9(U1_pin7));
  _7430 u_7430_2 (
    .pin1(q04), .pin2(q06), .pin3(q08), .pin4(q00), .pin5(n7430_1_pin5), .pin6(n7430_1_pin6), .pin12(q03),
    .pin11(n7430_1_pin11), .pin8(n7430_2_pin8));  // open: pin13, pin10, pin9
  // Probe on q05
  // Probe on q06
  // Probe on q07
  // Probe on q08
  _7430 u_7430_3 (
    .pin1(q04), .pin2(q06), .pin3(q08), .pin4(q00), .pin5(n7430_1_pin5), .pin6(n7430_3_pin6), .pin12(q03),
    .pin11(n7430_1_pin11), .pin8(n7430_3_pin8));  // open: pin13, pin10, pin9
  _7404 u_7404_1 (
    .pin1(q00), .pin2(n7430_1_pin4), .pin3(q01), .pin4(n7430_1_pin5), .pin5(q02), .pin6(n7430_1_pin6),
    .pin13(q03), .pin12(n7430_3_pin6), .pin9(q05), .pin8(n7430_1_pin11));  // open: pin11, pin10
  // Probe on q09
  _74161 U3 (
    .pin1(U1_pin1), .pin2(CLK), .pin3(DataBits), .pin4(DataBits), .pin5(DataBits), .pin6(DataBits),
    .pin7(U2_pin15), .pin14(q08), .pin13(q09), .pin10(U2_pin15), .pin9(U1_pin7));  // open: pin15, pin12, pin11
  _7430 u_7430_4 (
    .pin1(q04), .pin2(q06), .pin3(q08), .pin4(n7430_1_pin4), .pin5(n7430_1_pin5), .pin6(n7430_3_pin6),
    .pin12(q02), .pin11(q05), .pin8(U1_pin1));  // open: pin13, pin10, pin9
  _7400 u_7400_1 (
    .pin1(n7430_2_pin8), .pin2(VSync), .pin3(n7400_1_pin3), .pin4(n7400_1_pin3), .pin5(n7430_3_pin8),
    .pin6(VSync), .pin13(U1_pin1), .pin12(n7400_1_pin12), .pin11(VBlank), .pin10(n7430_1_pin8),
    .pin9(VBlank), .pin8(n7400_1_pin12));
  // also tied to VCC on the sheet: U1_pin7
endmodule

module EEPROM (
  input  in_1,
  input  in_2,
  input  in_3,
  input  in_4
);

  wire clock_1_out, horizontal_sync_1_bit264;
  wire [6:6] horizontal_sync_1_hsync, vertical_sync_1_vsync;
  wire [7:0] EEPROM_data;
  wire [13:0] horizontal_sync_1_q01;

  Clock clock_1 (.out(clock_1_out));
  Horizontal_Sync horizontal_sync_1 (
    .CLK(clock_1_out), .DataBits(in_1), .in_3(in_2), .HSync(horizontal_sync_1_hsync[6]),
    .Bit264(horizontal_sync_1_bit264), .q01(horizontal_sync_1_q01[0]), .q02(horizontal_sync_1_q01[1]),
    .q03(horizontal_sync_1_q01[2]), .q04(horizontal_sync_1_q01[3]), .q05(horizontal_sync_1_q01[4]),
    .q06(horizontal_sync_1_q01[5]), .q07(horizontal_sync_1_q01[6]));  // open: HBlank, q00, q08
  Vertical_Sync vertical_sync_1 (
    .CLK(horizontal_sync_1_bit264), .DataBits(in_1), .VSync(vertical_sync_1_vsync[6]),
    .q03(horizontal_sync_1_q01[7]), .q04(horizontal_sync_1_q01[8]), .q05(horizontal_sync_1_q01[9]),
    .q06(horizontal_sync_1_q01[10]), .q07(horizontal_sync_1_q01[11]), .q08(horizontal_sync_1_q01[12]),
    .q09(horizontal_sync_1_q01[13]));  // open: VBlank, q00, q01, q02
  ROM #(.addrWidth(15)) EEPROM (.addr({1'b0, horizontal_sync_1_q01}), .data(EEPROM_data));
  // RGB_Video rgb_video_1: pin names not known; wires that end beside it: in_3, clock_1_out, in_4, {7{horizontal_sync_1_hsync[6]}}, {7{vertical_sync_1_vsync[6]}}, EEPROM_data
endmodule
